// Logisim project CPU_but_how-16.circ as structural Verilog: 25 circuits, main circuit main
module main (
  input  in_1,
  input  in_2,
  output [15:0] out_3,
  output [15:0] out_4,
  output out_5
);

  Counter #(.width(16), .max('hffff)) counter_1 (
    .count(1'b1), .Q(out_3), .clk(in_2), .clr(in_1));  // open: load, D, carry
  not not_1 (out_5, in_2);
  ROM #(.addrWidth(16), .dataWidth(16)) rom_1 (.addr(out_3), .data(out_4));  // open: sel

  // Notes on the sheet:
  //   contents of rom_1 (hex, n*v repeats v):
  //   2222 333 170*0 3333 56*0 333 569*0 3333
endmodule

module CPU_MEM_1 (
  input  s,
  input  e,
  output out_3
);

  wire nand_1_out, nand_2_out, nand_4_out;

  nand nand_1 (nand_1_out, s, e);
  nand nand_2 (nand_2_out, nand_1_out, e);
  nand nand_3 (out_3, nand_1_out, nand_4_out);
  nand nand_4 (nand_4_out, out_3, nand_2_out);

  // Notes on the sheet:
  //   o
endmodule

module CPU_MEM_16 (
  input  [15:0] in_1,
  input  in_2,
  output [15:0] out_3
);

  CPU_MEM_1 cpu_mem_1_1 (.s(in_1[0]), .e(in_2), .out_3(out_3[0]));
  CPU_MEM_1 cpu_mem_1_2 (.s(in_1[1]), .e(in_2), .out_3(out_3[1]));
  CPU_MEM_1 cpu_mem_1_3 (.s(in_1[2]), .e(in_2), .out_3(out_3[2]));
  CPU_MEM_1 cpu_mem_1_4 (.s(in_1[3]), .e(in_2), .out_3(out_3[3]));
  CPU_MEM_1 cpu_mem_1_5 (.s(in_1[4]), .e(in_2), .out_3(out_3[4]));
  CPU_MEM_1 cpu_mem_1_6 (.s(in_1[5]), .e(in_2), .out_3(out_3[5]));
  CPU_MEM_1 cpu_mem_1_7 (.s(in_1[6]), .e(in_2), .out_3(out_3[6]));
  CPU_MEM_1 cpu_mem_1_8 (.s(in_1[7]), .e(in_2), .out_3(out_3[7]));
  CPU_MEM_1 cpu_mem_1_9 (.s(in_1[8]), .e(in_2), .out_3(out_3[8]));
  CPU_MEM_1 cpu_mem_1_10 (.s(in_1[9]), .e(in_2), .out_3(out_3[9]));
  CPU_MEM_1 cpu_mem_1_11 (.s(in_1[10]), .e(in_2), .out_3(out_3[10]));
  CPU_MEM_1 cpu_mem_1_12 (.s(in_1[11]), .e(in_2), .out_3(out_3[11]));
  CPU_MEM_1 cpu_mem_1_13 (.s(in_1[12]), .e(in_2), .out_3(out_3[12]));
  CPU_MEM_1 cpu_mem_1_14 (.s(in_1[13]), .e(in_2), .out_3(out_3[13]));
  CPU_MEM_1 cpu_mem_1_15 (.s(in_1[14]), .e(in_2), .out_3(out_3[14]));
  CPU_MEM_1 cpu_mem_1_16 (.s(in_1[15]), .e(in_2), .out_3(out_3[15]));

  // Notes on the sheet:
  //   in_2: pull=down
endmodule

module CPU_ENABLE_16 (
  input  [15:0] in_1,
  input  in_2,
  output [15:0] out_3
);

  wire and_1_out, and_2_out, and_3_out, and_4_out, and_5_out, and_6_out, and_7_out, and_8_out, and_9_out,
       and_10_out, and_11_out, and_12_out, and_13_out, and_14_out, and_15_out, and_16_out;

  and and_1 (and_1_out, in_1[0], in_2);
  and and_2 (and_2_out, in_1[1], in_2);
  and and_3 (and_3_out, in_1[2], in_2);
  and and_4 (and_4_out, in_1[3], in_2);
  and and_5 (and_5_out, in_1[4], in_2);
  and and_6 (and_6_out, in_1[5], in_2);
  and and_7 (and_7_out, in_1[6], in_2);
  and and_8 (and_8_out, in_1[7], in_2);
  and and_9 (and_9_out, in_1[8], in_2);
  and and_10 (and_10_out, in_1[9], in_2);
  and and_11 (and_11_out, in_1[10], in_2);
  and and_12 (and_12_out, in_1[11], in_2);
  and and_13 (and_13_out, in_1[12], in_2);
  and and_14 (and_14_out, in_1[13], in_2);
  and and_15 (and_15_out, in_1[14], in_2);
  and and_16 (and_16_out, in_1[15], in_2);
  assign out_3[0] = in_2 ? and_1_out : 1'bz;  // Controlled_Buffer controlled_buffer_1
  assign out_3[1] = in_2 ? and_2_out : 1'bz;  // Controlled_Buffer controlled_buffer_2
  assign out_3[2] = in_2 ? and_3_out : 1'bz;  // Controlled_Buffer controlled_buffer_3
  assign out_3[3] = in_2 ? and_4_out : 1'bz;  // Controlled_Buffer controlled_buffer_4
  assign out_3[4] = in_2 ? and_5_out : 1'bz;  // Controlled_Buffer controlled_buffer_5
  assign out_3[5] = in_2 ? and_6_out : 1'bz;  // Controlled_Buffer controlled_buffer_6
  assign out_3[6] = in_2 ? and_7_out : 1'bz;  // Controlled_Buffer controlled_buffer_7
  assign out_3[7] = in_2 ? and_8_out : 1'bz;  // Controlled_Buffer controlled_buffer_8
  assign out_3[8] = in_2 ? and_9_out : 1'bz;  // Controlled_Buffer controlled_buffer_9
  assign out_3[9] = in_2 ? and_10_out : 1'bz;  // Controlled_Buffer controlled_buffer_10
  assign out_3[10] = in_2 ? and_11_out : 1'bz;  // Controlled_Buffer controlled_buffer_11
  assign out_3[11] = in_2 ? and_12_out : 1'bz;  // Controlled_Buffer controlled_buffer_12
  assign out_3[12] = in_2 ? and_13_out : 1'bz;  // Controlled_Buffer controlled_buffer_13
  assign out_3[13] = in_2 ? and_14_out : 1'bz;  // Controlled_Buffer controlled_buffer_14
  assign out_3[14] = in_2 ? and_15_out : 1'bz;  // Controlled_Buffer controlled_buffer_15
  assign out_3[15] = in_2 ? and_16_out : 1'bz;  // Controlled_Buffer controlled_buffer_16

  // Notes on the sheet:
  //   i
  //   o
endmodule

module CPU_DECODER_3x8 (
  input  a,
  input  b,
  input  c,
  output _0,
  output _1,
  output _2,
  output _3,
  output _4,
  output _5,
  output _6,
  output _7
);

  wire not_1_out, not_2_out, not_3_out;

  not not_1 (not_1_out, a);
  not not_2 (not_2_out, b);
  not not_3 (not_3_out, c);
  and and_1 (_0, not_1_out, not_2_out, not_3_out);
  and and_2 (_1, not_1_out, not_2_out, c);
  and and_3 (_2, not_1_out, b, not_3_out);
  and and_4 (_3, not_1_out, b, c);
  and and_5 (_4, a, not_2_out, not_3_out);
  and and_6 (_5, a, c, not_2_out);
  and and_7 (_6, a, b, not_3_out);
  and and_8 (_7, a, b, c);
endmodule

module CPU_DECODER_2x4 (
  input  a,
  input  b,
  output _0,
  output _1,
  output _2,
  output _3
);

  wire not_1_out, not_2_out;

  not not_1 (not_1_out, a);
  not not_2 (not_2_out, b);
  and and_1 (_0, not_1_out, not_2_out);
  and and_2 (_1, not_1_out, b);
  and and_3 (_2, a, not_2_out);
  and and_4 (_3, b, a);
endmodule

module CPU_DECODER_4x16 (
  input  a,
  input  b,
  input  c,
  input  d,
  output _0,
  output _1,
  output _2,
  output _3,
  output _4,
  output _5,
  output _6,
  output _7,
  output _8,
  output _9,
  output a_2,
  output b_2,
  output c_2,
  output d_2,
  output e,
  output f
);

  wire not_1_out, not_2_out, not_3_out, not_4_out;

  not not_1 (not_1_out, a);
  not not_2 (not_2_out, b);
  not not_3 (not_3_out, c);
  not not_4 (not_4_out, d);
  and and_1 (_0, not_1_out, not_2_out, not_3_out, not_4_out);
  and and_2 (_1, not_1_out, not_2_out, not_3_out, d);
  and and_3 (_2, not_1_out, not_2_out, c, not_4_out);
  and and_4 (_3, not_1_out, not_2_out, c, d);
  and and_5 (_4, not_1_out, b, not_3_out, not_4_out);
  and and_6 (_5, not_1_out, b, not_3_out, d);
  and and_7 (_6, not_1_out, b, c, not_4_out);
  and and_8 (_7, not_1_out, b, c, d);
  and and_9 (_8, a, not_2_out, not_3_out, not_4_out);
  and and_10 (_9, a, not_2_out, not_3_out, d);
  and and_11 (a_2, a, not_2_out, c, not_4_out);
  and and_12 (b_2, a, not_2_out, c, d);
  and and_13 (c_2, a, b, not_3_out, not_4_out);
  and and_14 (d_2, a, b, not_3_out, d);
  and and_15 (e, a, b, c, not_4_out);
  and and_16 (f, a, b, c, d);
endmodule

module CPU_REGISTER_16 (
  input  [15:0] in_1,
  input  s,
  input  e,
  output [15:0] out_4,
  output [15:0] out_5
);

  wire [15:0] cpu_enable_16_1_out_3;

  CPU_MEM_16 cpu_mem_16_1 (.in_2(s), .in_1(in_1), .out_3(out_4));
  CPU_ENABLE_16 cpu_enable_16_1 (.in_1(out_4), .out_3(cpu_enable_16_1_out_3), .in_2(e));
  assign out_5 = e ? cpu_enable_16_1_out_3 : 16'bz;  // Controlled_Buffer controlled_buffer_1

  // Notes on the sheet:
  //   reg
  //   `
  //   o
endmodule

module CPU_REG_WORD (
  input  [15:0] in_1,
  input  h,
  input  v,
  input  reset,
  input  s,
  input  e,
  output [15:0] out_7,
  output [15:0] out_8
);

  wire and_1_out, and_2_out, and_3_out, or_1_out;
  wire [15:0] cpu_register_16_1_out_4, cpu_register_16_1_out_5;

  and and_1 (and_1_out, h, v);
  assign out_7 = and_2_out ? cpu_register_16_1_out_4 : 16'bz;  // Controlled_Buffer controlled_buffer_1
  and and_2 (and_2_out, and_1_out, s);
  and and_3 (and_3_out, and_1_out, e);
  or or_1 (or_1_out, and_2_out, reset);
  CPU_REGISTER_16 cpu_register_16_1 (
    .in_1(in_1), .s(or_1_out), .e(and_3_out), .out_5(cpu_register_16_1_out_5), .out_4(cpu_register_16_1_out_4));
  assign out_8 = and_3_out ? cpu_register_16_1_out_5 : 16'bz;  // Controlled_Buffer controlled_buffer_2

  // Notes on the sheet:
  //   reset: pull=down
endmodule

module CPU_RAM_32 (
  input  [7:0] in_1,
  input  sa,
  input  s,
  input  e,
  input  [7:0] in_5,
  input  r,
  output [7:0] out_7,
  output [7:0] out_8
);

  wire cpu_decoder_2x4_1__1, cpu_decoder_2x4_1__2, cpu_decoder_2x4_1__3, cpu_decoder_3x8_1__0,
       cpu_decoder_3x8_1__1, cpu_decoder_3x8_1__2, cpu_decoder_3x8_1__3, cpu_decoder_3x8_1__4,
       cpu_decoder_3x8_1__5, cpu_decoder_3x8_1__6, cpu_decoder_3x8_1__7, cpu_reg_word_1_p3;
  wire [7:0] cpu_mem_16_1_p3;

  // CPU_MEM_16 cpu_mem_16_1: pin names not known; wires that end beside it: in_1, sa, cpu_mem_16_1_p3
  CPU_DECODER_3x8 cpu_decoder_3x8_1 (
    ._0(cpu_decoder_3x8_1__0), ._1(cpu_decoder_3x8_1__1), ._2(cpu_decoder_3x8_1__2),
    ._3(cpu_decoder_3x8_1__3), ._4(cpu_decoder_3x8_1__4), ._5(cpu_decoder_3x8_1__5),
    ._6(cpu_decoder_3x8_1__6), ._7(cpu_decoder_3x8_1__7), .a(cpu_mem_16_1_p3[4]), .b(cpu_mem_16_1_p3[3]),
    .c(cpu_mem_16_1_p3[2]));
  // CPU_REG_WORD cpu_reg_word_1: pin names not known; wires that end beside it: cpu_decoder_3x8_1__0, in_5, cpu_reg_word_1_p3, s, out_8, e, r, out_7
  // CPU_REG_WORD cpu_reg_word_2: pin names not known; wires that end beside it: cpu_decoder_3x8_1__1, in_5, cpu_reg_word_1_p3, s, out_8, e, r, out_7
  // CPU_REG_WORD cpu_reg_word_3: pin names not known; wires that end beside it: cpu_decoder_3x8_1__2, in_5, cpu_reg_word_1_p3, s, out_8, e, r, out_7
  // CPU_REG_WORD cpu_reg_word_4: pin names not known; wires that end beside it: cpu_decoder_3x8_1__3, in_5, cpu_reg_word_1_p3, s, out_8, e, r, out_7
  // CPU_REG_WORD cpu_reg_word_5: pin names not known; wires that end beside it: cpu_decoder_3x8_1__4, in_5, cpu_reg_word_1_p3, s, out_8, e, r, out_7
  // CPU_REG_WORD cpu_reg_word_6: pin names not known; wires that end beside it: cpu_decoder_3x8_1__5, in_5, cpu_reg_word_1_p3, s, out_8, e, r, out_7
  // CPU_REG_WORD cpu_reg_word_7: pin names not known; wires that end beside it: cpu_decoder_3x8_1__6, in_5, cpu_reg_word_1_p3, s, out_8, e, r, out_7
  // CPU_REG_WORD cpu_reg_word_8: pin names not known; wires that end beside it: cpu_decoder_3x8_1__7, in_5, cpu_reg_word_1_p3, s, out_8, e, r, out_7
  CPU_DECODER_2x4 cpu_decoder_2x4_1 (
    .a(cpu_mem_16_1_p3[1]), .b(cpu_mem_16_1_p3[0]), ._0(cpu_reg_word_1_p3), ._1(cpu_decoder_2x4_1__1),
    ._2(cpu_decoder_2x4_1__2), ._3(cpu_decoder_2x4_1__3));
  // CPU_REG_WORD cpu_reg_word_9: pin names not known; wires that end beside it: cpu_decoder_3x8_1__0, in_5, cpu_decoder_2x4_1__1, s, out_8, e, r, out_7
  // CPU_REG_WORD cpu_reg_word_10: pin names not known; wires that end beside it: cpu_decoder_2x4_1__1, in_5, cpu_decoder_2x4_1__1, s, out_8, e, r, out_7
  // CPU_REG_WORD cpu_reg_word_11: pin names not known; wires that end beside it: cpu_decoder_3x8_1__2, in_5, cpu_decoder_2x4_1__1, s, out_8, e, r, out_7
  // CPU_REG_WORD cpu_reg_word_12: pin names not known; wires that end beside it: cpu_decoder_3x8_1__3, in_5, cpu_decoder_2x4_1__1, s, out_8, e, r, out_7
  // CPU_REG_WORD cpu_reg_word_13: pin names not known; wires that end beside it: cpu_decoder_3x8_1__4, in_5, cpu_decoder_2x4_1__1, s, out_8, e, r, out_7
  // CPU_REG_WORD cpu_reg_word_14: pin names not known; wires that end beside it: cpu_decoder_3x8_1__5, in_5, cpu_decoder_2x4_1__1, s, out_8, e, r, out_7
  // CPU_REG_WORD cpu_reg_word_15: pin names not known; wires that end beside it: cpu_decoder_3x8_1__6, in_5, cpu_decoder_2x4_1__1, s, out_8, e, r, out_7
  // CPU_REG_WORD cpu_reg_word_16: pin names not known; wires that end beside it: cpu_decoder_3x8_1__7, in_5, cpu_decoder_2x4_1__1, s, out_8, e, r, out_7
  // CPU_REG_WORD cpu_reg_word_17: pin names not known; wires that end beside it: cpu_decoder_3x8_1__0, in_5, cpu_decoder_2x4_1__2, s, out_8, e, r, out_7
  // CPU_REG_WORD cpu_reg_word_18: pin names not known; wires that end beside it: cpu_decoder_3x8_1__1, in_5, cpu_decoder_2x4_1__2, s, out_8, e, r, out_7
  // CPU_REG_WORD cpu_reg_word_19: pin names not known; wires that end beside it: cpu_decoder_3x8_1__2, in_5, cpu_decoder_2x4_1__2, s, out_8, e, r, out_7
  // CPU_REG_WORD cpu_reg_word_20: pin names not known; wires that end beside it: cpu_decoder_3x8_1__3, in_5, cpu_decoder_2x4_1__2, s, out_8, e, r, out_7
  // CPU_REG_WORD cpu_reg_word_21: pin names not known; wires that end beside it: cpu_decoder_3x8_1__4, in_5, cpu_decoder_2x4_1__2, s, out_8, e, r, out_7
  // CPU_REG_WORD cpu_reg_word_22: pin names not known; wires that end beside it: cpu_decoder_3x8_1__5, in_5, cpu_decoder_2x4_1__2, s, out_8, e, r, out_7
  // CPU_REG_WORD cpu_reg_word_23: pin names not known; wires that end beside it: cpu_decoder_3x8_1__6, in_5, cpu_decoder_2x4_1__2, s, out_8, e, r, out_7
  // CPU_REG_WORD cpu_reg_word_24: pin names not known; wires that end beside it: cpu_decoder_3x8_1__7, in_5, cpu_decoder_2x4_1__2, s, out_8, e, r, out_7
  // CPU_REG_WORD cpu_reg_word_25: pin names not known; wires that end beside it: cpu_decoder_3x8_1__0, in_5, cpu_decoder_2x4_1__3, s, out_8, e, r, out_7
  // CPU_REG_WORD cpu_reg_word_26: pin names not known; wires that end beside it: cpu_decoder_3x8_1__1, in_5, cpu_decoder_2x4_1__3, s, out_8, e, r, out_7
  // CPU_REG_WORD cpu_reg_word_27: pin names not known; wires that end beside it: cpu_decoder_3x8_1__2, in_5, cpu_decoder_2x4_1__3, s, out_8, e, r, out_7
  // CPU_REG_WORD cpu_reg_word_28: pin names not known; wires that end beside it: cpu_decoder_3x8_1__3, in_5, cpu_decoder_2x4_1__3, s, out_8, e, r, out_7
  // CPU_REG_WORD cpu_reg_word_29: pin names not known; wires that end beside it: cpu_decoder_3x8_1__4, in_5, cpu_decoder_2x4_1__3, s, out_8, e, r, out_7
  // CPU_REG_WORD cpu_reg_word_30: pin names not known; wires that end beside it: cpu_decoder_3x8_1__5, in_5, cpu_decoder_2x4_1__3, s, out_8, e, r, out_7
  // CPU_REG_WORD cpu_reg_word_31: pin names not known; wires that end beside it: cpu_decoder_3x8_1__6, in_5, cpu_decoder_2x4_1__3, s, out_8, e, r, out_7
  // CPU_REG_WORD cpu_reg_word_32: pin names not known; wires that end beside it: cpu_decoder_3x8_1__7, in_5, cpu_decoder_2x4_1__3, s, out_8, e, r, out_7

  // Notes on the sheet:
  //   address
  //   i
  //   o
  //   reg
endmodule

module CPU_ADDER (
  input  a,
  input  b,
  input  cin,
  output sum,
  output cout
);

  wire and_1_out, and_2_out, xor_1_out;

  xor xor_1 (xor_1_out, a, b);
  and and_1 (and_1_out, cin, xor_1_out);
  and and_2 (and_2_out, a, b);
  xor xor_2 (sum, xor_1_out, cin);
  or or_1 (cout, and_1_out, and_2_out);
endmodule

module CPU_ADDER_16 (
  input  cin,
  input  [15:0] in_2,
  input  [15:0] in_3,
  output [15:0] out_4,
  output out_5
);

  Adder #(.width(16)) adder_1 (.a(in_2), .b(in_3), .out(out_4), .cin(cin), .cout(out_5));

  // Notes on the sheet:
  //   a
  //   b
endmodule

module CPU_ALU (
  input  [15:0] in_1,
  input  in_2,
  input  [15:0] in_3,
  input  in_4,
  input  s1,
  input  s2,
  input  s3,
  output z,
  output [15:0] out_9,
  output [15:0] out_10,
  output [15:0] out_11,
  output out_12
);

  wire cpu_adder_16_1_out_5, cpu_decoder_3x8_1__0, cpu_decoder_3x8_1__1, cpu_decoder_3x8_1__2,
       cpu_decoder_3x8_1__3, cpu_decoder_3x8_1__4, cpu_decoder_3x8_1__5, cpu_decoder_3x8_1__6,
       cpu_decoder_3x8_1__7, multiplexer_1_out, multiplexer_2_out, not_2_out, not_3_out, subtractor_1_bout;
  wire [15:0] A, and_1_out, B, cpu_adder_16_1_out_4, not_1_out, or_1_out, shifter_1_out, shifter_2_out,
       subtractor_1_out, xor_1_out;

  CPU_REGISTER_16 cpu_register_16_1 (.in_1(in_1), .s(in_2), .e(1'b1), .out_5(A), .out_4(out_9));
  CPU_REGISTER_16 cpu_register_16_2 (.in_1(in_3), .s(in_4), .e(1'b1), .out_5(B), .out_4(out_11));
  Shifter #(.width(16), .shift("lr")) shifter_1 (.in(A), .\dist (B[3:0]), .out(shifter_1_out));
  Shifter #(.width(16)) shifter_2 (.in(A), .\dist (B[3:0]), .out(shifter_2_out));
  assign xor_1_out = A ^ B;  // XOR_Gate xor_1, 16 bits wide
  assign or_1_out = B | B;  // OR_Gate or_1, 16 bits wide
  assign and_1_out = B & A;  // AND_Gate and_1, 16 bits wide
  assign not_1_out = ~A;  // NOT_Gate not_1, 16 bits wide
  CPU_ADDER_16 cpu_adder_16_1 (
    .in_2(A), .out_4(cpu_adder_16_1_out_4), .in_3(B), .out_5(cpu_adder_16_1_out_5));  // open: cin
  Subtractor #(.width(16)) subtractor_1 (.a(A), .b(B), .out(subtractor_1_out), .bout(subtractor_1_bout));  // open: bin
  assign out_10 = cpu_decoder_3x8_1__0 ? cpu_adder_16_1_out_4 : 16'bz;  // Controlled_Buffer controlled_buffer_1
  CPU_DECODER_3x8 cpu_decoder_3x8_1 (
    ._0(cpu_decoder_3x8_1__0), ._1(cpu_decoder_3x8_1__1), ._2(cpu_decoder_3x8_1__2),
    ._3(cpu_decoder_3x8_1__3), ._4(cpu_decoder_3x8_1__4), ._5(cpu_decoder_3x8_1__5),
    ._6(cpu_decoder_3x8_1__6), ._7(cpu_decoder_3x8_1__7), .a(s1), .b(s2), .c(s3));
  assign out_10 = cpu_decoder_3x8_1__3 ? or_1_out : 16'bz;  // Controlled_Buffer controlled_buffer_2
  assign out_10 = cpu_decoder_3x8_1__2 ? and_1_out : 16'bz;  // Controlled_Buffer controlled_buffer_3
  assign out_10 = cpu_decoder_3x8_1__1 ? not_1_out : 16'bz;  // Controlled_Buffer controlled_buffer_4
  assign out_10 = cpu_decoder_3x8_1__6 ? shifter_1_out : 16'bz;  // Controlled_Buffer controlled_buffer_5
  assign out_10 = cpu_decoder_3x8_1__5 ? shifter_2_out : 16'bz;  // Controlled_Buffer controlled_buffer_6
  assign out_10 = cpu_decoder_3x8_1__4 ? xor_1_out : 16'bz;  // Controlled_Buffer controlled_buffer_7
  assign out_10 = cpu_decoder_3x8_1__7 ? subtractor_1_out : 16'bz;  // Controlled_Buffer controlled_buffer_8
  not not_2 (not_2_out, cpu_decoder_3x8_1__0);
  Multiplexer multiplexer_1 (
    .in0(subtractor_1_bout), .in1(1'b0), .out(multiplexer_1_out), .sel(not_3_out));  // open: en
  not not_3 (not_3_out, cpu_decoder_3x8_1__7);
  Multiplexer multiplexer_2 (
    .in0(cpu_adder_16_1_out_5), .in1(1'b0), .out(multiplexer_2_out), .sel(not_2_out));  // open: en
  or or_2 (out_12, multiplexer_2_out, multiplexer_1_out);
  nor nor_1 (z, out_10[0], out_10[1], out_10[2], out_10[3], out_10[4], out_10[5], out_10[6], out_10[7], out_10[8], out_10[9], out_10[10], out_10[11], out_10[12], out_10[13], out_10[14], out_10[15]);

  // Notes on the sheet:
  //   in_3: pull=down
  //   in_1: pull=down
endmodule

module CPU_PC (
  input  CE,
  input  [15:0] in_2,
  input  J,
  input  cp,
  input  in_5,
  input  R,
  output [15:0] out_7,
  output [15:0] out_8
);

  wire [15:0] counter_1_q;

  Counter #(.width(16), .max('hffff)) counter_1 (
    .load(J), .D(in_2), .count(CE), .Q(counter_1_q), .clk(cp), .clr(R));  // open: carry
  CPU_REG cpu_reg_1 (.in_1(counter_1_q), .s(1'b1), .e(in_5), .out_4(out_7), .out_5(out_8));

  // Notes on the sheet:
  //   R: pull=down
  //   cp: pull=down
  //   CE: pull=down
  //   CE = J = 1 : 计数器递减
  //   CE=1 J=0   计数器递增
  //   CE=0 J=1 Load模式
endmodule

module CPU_MEM_256 (
  input  in_1,
  input  sa,
  input  in_3,
  input  [15:0] in_4,
  input  [15:0] in_5,
  input  [15:0] in_6,
  input  in_7,
  input  [15:0] in_8,
  input  in_9,
  input  in_10,
  input  in_11,
  input  in_12,
  input  in_13,
  input  in_14,
  output [15:0] out_15,
  output [15:0] out_16
);

  wire CP, MI, MO, not_1_out, SA_t;
  wire [15:0] ADDR, cpu_reg_1_out_5, cpu_reg_2_out_5, DAT;

  CPU_REG cpu_reg_1 (.in_1(ADDR), .s(SA_t), .e(1'b1), .out_5(cpu_reg_1_out_5));  // open: out_4
  CPU_REG cpu_reg_2 (.in_1(DAT), .s(MI), .e(1'b1), .out_5(cpu_reg_2_out_5));  // open: out_4
  Multiplexer multiplexer_1 (.in0(sa), .in1(in_3), .out(SA_t), .sel(in_7));  // open: en
  Multiplexer #(.width(16)) multiplexer_2 (.in0(in_4), .in1(in_5), .out(ADDR), .sel(in_7));  // open: en
  Multiplexer #(.width(16)) multiplexer_3 (.in0(in_6), .in1(in_8), .out(DAT), .sel(in_7));  // open: en
  Multiplexer multiplexer_4 (.in0(in_9), .in1(in_10), .out(MI), .sel(in_7));  // open: en
  Multiplexer multiplexer_5 (.in0(in_11), .in1(in_12), .out(MO), .sel(in_7));  // open: en
  Multiplexer multiplexer_6 (.in0(in_13), .in1(in_14), .out(CP), .sel(in_7));  // open: en
  RAM #(.addrWidth(16), .dataWidth(16), .bus("separate")) ram_1 (
    .addr(cpu_reg_1_out_5), .din(cpu_reg_2_out_5), .data(out_15), .str(MI), .sel(1'b1), .clk(CP), .ld(MO),
    .clr(in_1));
  assign out_16 = not_1_out ? out_15 : 16'bz;  // Controlled_Buffer controlled_buffer_1
  not not_1 (not_1_out, in_7);

  // Other names for the same wires on the sheet: HAND = in_7

  // Notes on the sheet:
  //   in_1: pull=down
  //   hand
endmodule

module CPU (
  input  in_1,
  input  RESET,
  input  in_3,
  input  LD,
  input  [15:0] in_5,
  input  [15:0] in_6,
  input  MEM_HAND_INPUT,
  input  CT,
  input  [15:0] in_9,
  output [2:0] out_10
);

  wire CLK, CLK_2_out, CLK_out, comparator_1_lt, CP, cpu_control_1_out_7, cpu_control_1_out_8,
       cpu_control_1_out_9, cpu_control_1_out_10, cpu_control_1_out_12, cpu_control_1_out_13,
       cpu_control_1_out_14, cpu_control_1_out_16, cpu_control_1_out_17, cpu_control_1_out_18,
       cpu_control_1_out_19, cpu_control_1_out_20, cpu_control_1_out_21, cpu_control_1_out_23,
       multiplexer_1_out, not_1_out, not_2_out, SL_E;
  wire [1:0] FLAGS;
  wire [3:0] cpu_control_1_rx_e, cpu_control_1_rx_s, FLAG_C;
  wire [6:0] OUT_SERL;
  wire [15:0] cpu_alu_1_out_9, cpu_alu_1_out_10, cpu_alu_1_out_11, cpu_ir_1_out_4, cpu_pc_1_out_7,
       cpu_regs_1_out_7, cpu_regs_1_out_8, cpu_regs_1_out_9, cpu_regs_1_out_10, cpu_regs_1_out_11,
       cpu_regs_1_out_12, cpu_regs_1_out_13, cpu_regs_1_out_14, cpu_regs_1_out_15, cpu_regs_1_out_16,
       cpu_regs_1_out_17, cpu_regs_1_out_19, cpu_regs_1_out_20, MA, MD, RAM_O;
  wire [15:7] controlled_buffer_1_out;

  Clock u_CLK (.out(CLK_out));
  not not_1 (not_1_out, cpu_control_1_out_23);
  // Probe on cpu_pc_1_out_7
  assign {controlled_buffer_1_out, OUT_SERL} = in_3 ? in_5 : 16'bz;  // Controlled_Buffer controlled_buffer_1
  Multiplexer multiplexer_1 (.in0(not_1_out), .in1(1'b0), .out(multiplexer_1_out), .sel(MEM_HAND_INPUT));  // open: en
  CPU_PC cpu_pc_1 (
    .out_8({controlled_buffer_1_out, OUT_SERL}), .CE(cpu_control_1_out_12),
    .in_2({controlled_buffer_1_out, OUT_SERL}), .J(cpu_control_1_out_14), .R(RESET),
    .in_5(cpu_control_1_out_13), .cp(CLK), .out_7(cpu_pc_1_out_7));
  and and_1 (CLK, CLK_out, multiplexer_1_out);
  // Probe on cpu_ir_1_out_4
  not not_2 (not_2_out, CLK);
  CPU_IR cpu_ir_1 (
    .in_1({controlled_buffer_1_out, OUT_SERL}), .in_2(cpu_control_1_out_7), .out_4(cpu_ir_1_out_4));  // open: out_5, in_3
  // Probe on cpu_alu_1_out_9
  // Probe on cpu_alu_1_out_11
  // Probe on RAM_O
  CPU_MEM_256 cpu_mem_256_1 (
    .out_16({controlled_buffer_1_out, OUT_SERL}), .in_7(MEM_HAND_INPUT),
    .in_4({controlled_buffer_1_out, OUT_SERL}), .in_5(MA), .in_6({controlled_buffer_1_out, OUT_SERL}),
    .in_8(MD), .in_9(cpu_control_1_out_9), .in_10(1'b1), .in_11(cpu_control_1_out_10), .in_12(1'b1),
    .sa(cpu_control_1_out_8), .in_3(1'b1), .in_13(CLK), .in_14(CP), .out_15(RAM_O));  // open: in_1
  Comparator #(.width(16), .mode("unsigned")) comparator_1 (.a(in_9), .b(MA), .lt(comparator_1_lt));  // open: gt, eq
  CPU_CONTROL cpu_control_1 (
    .cp(not_2_out), .z(FLAG_C[1]), .c(FLAG_C[0]), .out_14(cpu_control_1_out_14),
    .out_16(cpu_control_1_out_16), .out_17(cpu_control_1_out_17), .out_18(cpu_control_1_out_18),
    .out_19(cpu_control_1_out_19), .out_20(cpu_control_1_out_20), .out_21(cpu_control_1_out_21),
    .out_22(SL_E), .out_23(cpu_control_1_out_23), .out_6(out_10), .in_4(cpu_ir_1_out_4),
    .out_7(cpu_control_1_out_7), .out_8(cpu_control_1_out_8), .out_9(cpu_control_1_out_9),
    .out_10(cpu_control_1_out_10), .out_12(cpu_control_1_out_12), .out_13(cpu_control_1_out_13),
    .in_1(RESET), .RX_S(cpu_control_1_rx_s), .RX_E(cpu_control_1_rx_e));
  Counter #(.width(16), .max('hffff)) counter_1 (
    .load(LD), .D(in_6), .count(CT), .Q(MA), .clk(CLK_2_out), .clr(comparator_1_lt));  // open: carry
  Clock CLK_2 (.out(CLK_2_out));
  CPU_ALU cpu_alu_1 (
    .s1(cpu_control_1_out_19), .s2(cpu_control_1_out_20), .s3(cpu_control_1_out_21), .z(FLAGS[1]),
    .in_2(cpu_control_1_out_16), .in_4(cpu_control_1_out_17), .in_3({controlled_buffer_1_out, OUT_SERL}),
    .out_11(cpu_alu_1_out_11), .in_1({controlled_buffer_1_out, OUT_SERL}), .out_9(cpu_alu_1_out_9),
    .out_10(cpu_alu_1_out_10), .out_12(FLAGS[0]));
  not not_3 (CP, CLK_2_out);
  // Probe on cpu_regs_1_out_20
  // Probe on cpu_regs_1_out_7
  ROM #(.addrWidth(16), .dataWidth(16)) rom_1 (.addr(MA), .data(MD));  // open: sel
  // Probe on cpu_regs_1_out_19
  // Probe on cpu_regs_1_out_17
  // Probe on cpu_regs_1_out_8
  // Probe on cpu_regs_1_out_9
  // Probe on OUT_SERL
  CPU_R cpu_r_1 (
    .in_1(cpu_alu_1_out_10), .out_5({controlled_buffer_1_out, OUT_SERL}), .in_2(1'b1),
    .in_3(cpu_control_1_out_18));  // open: out_4
  // Probe on cpu_regs_1_out_16
  // Probe on cpu_regs_1_out_15
  // Probe on cpu_regs_1_out_11
  // Probe on cpu_regs_1_out_10
  TTY tty_1 (.data(OUT_SERL), .clk(CLK), .we(SL_E), .clr(in_1));
  // Probe on cpu_regs_1_out_14
  // Probe on cpu_regs_1_out_13
  CPU_REGS cpu_regs_1 (
    .in_1({controlled_buffer_1_out, OUT_SERL}), .out_6({controlled_buffer_1_out, OUT_SERL}),
    .R_S(cpu_control_1_rx_s), .R_E(cpu_control_1_rx_e), .FLAG_I({2'b00, FLAGS}), .FLAG_O(FLAG_C),
    .out_7(cpu_regs_1_out_7), .out_8(cpu_regs_1_out_8), .out_9(cpu_regs_1_out_9), .out_10(cpu_regs_1_out_10),
    .out_11(cpu_regs_1_out_11), .out_12(cpu_regs_1_out_12), .out_13(cpu_regs_1_out_13),
    .out_14(cpu_regs_1_out_14), .out_15(cpu_regs_1_out_15), .out_16(cpu_regs_1_out_16),
    .out_17(cpu_regs_1_out_17), .out_19(cpu_regs_1_out_19), .out_20(cpu_regs_1_out_20));  // open: FLAG_BUS_I
  // Probe on cpu_regs_1_out_12

  // Other names for the same wires on the sheet: H = MEM_HAND_INPUT; WRITERA[15:0] = MA

  // Notes on the sheet:
  //   in_6: pull=down
  //   in_1: pull=down
  //   MEM WRITER
  //   MAX_ADDRESS
  //   contents of rom_1 (hex, n*v repeats v):
  //   50 7f 30 1 20 0 1220 823 1325 502 4 500 6 6 922 a11 b12 c30 d23 e23 f13 10 19 410 600 500 1c 600 10
  //   3 20 4 912 502 1b 911 502 27 600 20 ff00 30 4 832 501 26 832 501 32 600 812 80 18 1000 208 20 30
  //   1220 600 453*0 3 4 5 6 4*0 812 1100
endmodule

module CPU_REG (
  input  [15:0] in_1,
  input  s,
  input  e,
  output [15:0] out_4,
  output [15:0] out_5
);

  wire [15:0] cpu_enable_16_1_out_3;

  CPU_MEM_16 cpu_mem_16_1 (.in_2(s), .in_1(in_1), .out_3(out_4));
  CPU_ENABLE_16 cpu_enable_16_1 (.in_1(out_4), .out_3(cpu_enable_16_1_out_3), .in_2(e));
  assign out_5 = e ? cpu_enable_16_1_out_3 : 16'bz;  // Controlled_Buffer controlled_buffer_1

  // Notes on the sheet:
  //   reg
  //   `
  //   o
endmodule

module CPU_ROM (
  input  [7:0] in_1,
  input  rmo,
  input  rma,
  output [7:0] out_4
);

  wire [7:0] cpu_reg_1_p4, rom_1_data;

  // CPU_REG cpu_reg_1: pin names not known; wires that end beside it: in_1, rma, 1'b1, cpu_reg_1_p4
  ROM rom_1 (.addr(cpu_reg_1_p4), .data(rom_1_data), .sel(1'b1));
  // CPU_REG cpu_reg_2: pin names not known; wires that end beside it: rom_1_data, 1'b1, rmo, out_4

  // Notes on the sheet:
  //   contents of rom_1 (hex, n*v repeats v):
  //   0 21 61 e 2d 60 6 7 8 9 a b c d e f
endmodule

module CPU_IR (
  input  [15:0] in_1,
  input  in_2,
  input  in_3,
  output [15:0] out_4,
  output [15:0] out_5
);

  CPU_REGISTER_16 cpu_register_16_1 (.in_1(in_1), .s(in_2), .e(1'b1), .out_5(out_4));  // open: out_4
  assign out_5 = in_3 ? out_4 : 16'bz;  // Controlled_Buffer controlled_buffer_1

  // Notes on the sheet:
  //   IR_OE
endmodule

module CPU_R (
  input  [15:0] in_1,
  input  in_2,
  input  in_3,
  output [15:0] out_4,
  output [15:0] out_5
);

  CPU_REGISTER_16 cpu_register_16_1 (.in_1(in_1), .s(in_2), .e(in_3), .out_5(out_5), .out_4(out_4));

  // Notes on the sheet:
  //   in_2: pull=down
  //   in_3: pull=down
endmodule

module CPU_CONTROL (
  input  in_1,
  input  cp,
  input  z,
  input  [15:0] in_4,
  input  c,
  output [2:0] out_6,
  output out_7,
  output out_8,
  output out_9,
  output out_10,
  output [3:0] RX_S,
  output out_12,
  output out_13,
  output out_14,
  output [3:0] RX_E,
  output out_16,
  output out_17,
  output out_18,
  output out_19,
  output out_20,
  output out_21,
  output out_22,
  output out_23
);

  wire [23:15] rom_1_data;

  Counter #(.width(3), .max('h7)) counter_1 (
    .load(1'b0), .count(1'b1), .Q(out_6), .clk(cp), .clr(in_1));  // open: D, carry
  // Probe on {in_4, out_6, z, c}
  ROM #(.addrWidth(21), .dataWidth(32)) rom_1 (
    .addr({in_4, out_6, z, c}),
    .data({RX_S, RX_E, rom_1_data, out_23, out_22, out_21, out_20, out_19, out_18, out_17, out_16, out_14, out_13, out_12, out_10, out_9, out_8, out_7}));  // open: sel

  // Notes on the sheet:
  //   cp: pull=up
  //   c: pull=down
  //   in_1: pull=down
  //   in_4: pull=down
  //   z: pull=down
  //   ins
  //   contents of rom_1 (hex, n*v repeats v):
  //   4*22 4*9 4*10 4*22 4*8 4*10 8*0 4*22 4*9 4*10 4*22 4*8 4*10 8*0 4*22 4*9 4*10 4*22 4*8 4*10 8*0 4*22
  //   4*9 4*10 4*22 4*8 4*10 8*0 4*22 4*9 4*10 4*22 4*8 4*10 8*0 4*22 4*9 4*10 4*22 4*8 4*10 8*0 4*22 4*9
  //   4*10 4*22 4*8 4*10 8*0 4*22 4*9 4*10 4*22 4*8 4*10 8*0 4*22 4*9 4*10 4*22 4*8 4*10 8*0 4*22 4*9 4*10
  //   4*22 4*8 4*10 8*0 4*22 4*9 4*10 4*22 4*8 4*10 8*0 4*22 4*9 4*10 4*22 4*8 4*10 8*0 4*22 4*9 4*10 4*22
  //   4*8 4*10 8*0 4*22 4*9 4*10 4*22 4*8 4*10 8*0 4*22 4*9 4*10 4*22 4*8 4*10 8*0 4*22 4*9 4*10 4*22 4*8
  //   4*10 8*0 4*22 4*9 4*10 4*22 4*10000008 4*10 8*0 4*22 4*9 4*10 4*22 4*10000008 4*10 8*0 4*22 4*9 4*10
  //   4*22 4*10000008 4*10 8*0 4*22 4*9 4*10 4*22 4*10000008 4*10 8*0 4*22 4*9 4*10 4*22 4*10000008 4*10
  //   8*0 4*22 4*9 4*10 4*22 4*10000008 4*10 8*0 4*22 4*9 4*10 4*22 4*10000008 4*10 8*0 4*22 4*9 4*10 4*22
  //   4*10000008 4*10 8*0 4*22 4*9 4*10 4*22 4*10000008 4*10 8*0 4*22 4*9 4*10 4*22 4*10000008 4*10 8*0
  //   4*22 4*9 4*10 4*22 4*10000008 4*10 8*0 4*22 4*9 4*10 4*22 4*10000008 4*10 8*0 4*22 4*9 4*10 4*22
  //   4*10000008 4*10 8*0 4*22 4*9 4*10 4*22 4*10000008 4*10 8*0 4*22 4*9 4*10 4*22 4*10000008 4*10 8*0
  //   4*22 4*9 4*10 4*22 4*10000008 4*10 8*0 4*22 4*9 4*10 4*22 4*20000008 4*10 8*0 4*22 4*9 4*10 4*22
  //   4*20000008 4*10 8*0 4*22 4*9 4*10 4*22 4*20000008 4*10 8*0 4*22 4*9 4*10 4*22 4*20000008 4*10 8*0
  //   4*22 4*9 4*10 4*22 4*20000008 4*10 8*0 4*22 4*9 4*10 4*22 4*20000008 4*10 8*0 4*22 4*9 4*10 4*22
  //   4*20000008 4*10 8*0 4*22 4*9 4*10 4*22 4*20000008 4*10 8*0 4*22 4*9 4*10 4*22 4*20000008 4*10 8*0
  //   4*22 4*9 4*10 4*22 4*20000008 4*10 8*0 4*22 4*9 4*10 4*22 4*20000008 4*10 8*0 4*22 4*9 4*10 4*22
  //   4*20000008 4*10 8*0 4*22 4*9 4*10 4*22 4*20000008 4*10 8*0 4*22 4*9 4*10 4*22 4*20000008 4*10 8*0
  //   4*22 4*9 4*10 4*22 4*20000008 4*10 8*0 4*22 4*9 4*10 4*22 4*20000008 4*10 8*0 4*22 4*9 4*10 4*22
  //   4*30000008 4*10 8*0 4*22 4*9 4*10 4*22 4*30000008 4*10 8*0 4*22 4*9 4*10 4*22 4*30000008 4*10 8*0
  //   4*22 4*9 4*10 4*22 4*30000008 4*10 8*0 4*22 4*9 4*10 4*22 4*30000008 4*10 8*0 4*22 4*9 4*10 4*22
  //   4*30000008 4*10 8*0 4*22 4*9 4*10 4*22 4*30000008 4*10 8*0 4*22 4*9 4*10 4*22 4*30000008 4*10 8*0
  //   4*22 4*9 4*10 4*22 4*30000008 4*10 8*0 4*22 4*9 4*10 4*22 4*30000008 4*10 8*0 4*22 4*9 4*10 4*22
  //   4*30000008 4*10 8*0 4*22 4*9 4*10 4*22 4*30000008 4*10 8*0 4*22 4*9 4*10 4*22 4*30000008 4*10 8*0
  //   4*22 4*9 4*10 4*22 4*30000008 4*10 8*0 4*22 4*9 4*10 4*22 4*30000008 4*10 8*0 4*22 4*9 4*10 4*22
  //   4*30000008 4*10 8*0 4*22 4*9 4*10 4*22 4*40000008 4*10 8*0 4*22 4*9 4*10 4*22 4*40000008 4*10 8*0
  //   4*22 4*9 4*10 4*22 4*40000008 4*10 8*0 4*22 4*9 4*10 4*22 4*40000008 4*10 8*0 4*22 4*9 4*10 4*22
  //   4*40000008 4*10 8*0 4*22 4*9 4*10 4*22 4*40000008 4*10 8*0 4*22 4*9 4*10 4*22 4*40000008 4*10 8*0
  //   4*22 4*9 4*10 4*22 4*40000008 4*10 8*0 4*22 4*9 4*10 4*22 4*40000008 4*10 8*0 4*22 4*9 4*10 4*22
  //   4*40000008 4*10 8*0 4*22 4*9 4*10 4*22 4*40000008 4*10 8*0 4*22 4*9 4*10 4*22 4*40000008 4*10 8*0
  //   4*22 4*9 4*10 4*22 4*40000008 4*10 8*0 4*22 4*9 4*10 4*22 4*40000008 4*10 8*0 4*22 4*9 4*10 4*22
  //   4*40000008 4*10 8*0 4*22 4*9 4*10 4*22 4*40000008 4*10 8*0 4*22 4*9 4*10 4*22 4*50000008 4*10 8*0
  //   4*22 4*9 4*10 4*22 4*50000008 4*10 8*0 4*22 4*9 4*10 4*22 4*50000008 4*10 8*0 4*22 4*9 4*10 4*22
  //   4*50000008 4*10 8*0 4*22 4*9 4*10 4*22 4*50000008 4*10 8*0 4*22 4*9 4*10 4*22 4*50000008 4*10 8*0
  //   4*22 4*9 4*10 4*22 4*50000008 4*10 8*0 4*22 4*9 4*10 4*22 4*50000008 4*10 8*0 4*22 4*9 4*10 4*22
  //   4*50000008 4*10 8*0 4*22 4*9 4*10 4*22 4*50000008 4*10 8*0 4*22 4*9 4*10 4*22 4*50000008 4*10 8*0
  //   4*22 4*9 4*10 4*22 4*50000008 4*10 8*0 4*22 4*9 4*10 4*22 4*50000008 4*10 8*0 4*22 4*9 4*10 4*22
  //   4*50000008 4*10 8*0 4*22 4*9 4*10 4*22 4*50000008 4*10 8*0 4*22 4*9 4*10 4*22 4*50000008 4*10 8*0
  //   4*22 4*9 4*10 4*22 4*60000008 4*10 8*0 4*22 4*9 4*10 4*22 4*60000008 4*10 8*0 4*22 4*9 4*10 4*22
  //   4*60000008 4*10 8*0 4*22 4*9 4*10 4*22 4*60000008 4*10 8*0 4*22 4*9 4*10 4*22 4*60000008 4*10 8*0
  //   4*22 4*9 4*10 4*22 4*60000008 4*10 8*0 4*22 4*9 4*10 4*22 4*60000008 4*10 8*0 4*22 4*9 4*10 4*22
  //   4*60000008 4*10 8*0 4*22 4*9 4*10 4*22 4*60000008 4*10 8*0 4*22 4*9 4*10 4*2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
endmodule

module DIGITAL (
  input  [7:0] in_1,
  output [3:0] out_2,
  output [3:0] ONE_H,
  output [3:0] TEN_L,
  output [3:0] TEN_H,
  output [3:0] HUN_L,
  output [3:0] HUN_L_2
);

  _7_Segment_Display u_7_segment_display_1 (
    .g(HUN_L_2[3]), .f(HUN_L_2[2]), .a(HUN_L_2[1]), .b(HUN_L_2[0]), .e(HUN_L[3]), .d(HUN_L[2]), .c(HUN_L[1]),
    .dp(HUN_L[0]));
  // Probe on in_1
  _7_Segment_Display u_7_segment_display_2 (
    .g(TEN_H[3]), .f(TEN_H[2]), .a(TEN_H[1]), .b(TEN_H[0]), .e(TEN_L[3]), .d(TEN_L[2]), .c(TEN_L[1]),
    .dp(TEN_L[0]));
  ROM rom_1 (.addr(in_1), .data({ONE_H, out_2}));  // open: sel
  ROM rom_2 (.addr(in_1), .data({TEN_H, TEN_L}));  // open: sel
  ROM rom_3 (.addr(in_1), .data({HUN_L_2, HUN_L}));  // open: sel
  _7_Segment_Display u_7_segment_display_3 (
    .g(ONE_H[3]), .f(ONE_H[2]), .a(ONE_H[1]), .b(ONE_H[0]), .e(out_2[3]), .d(out_2[2]), .c(out_2[1]),
    .dp(out_2[0]));

  // Other names for the same wires on the sheet: HUN[7:0] = {HUN_L_2, HUN_L}; ONE[7:0] = {ONE_H, out_2};
  //   TEN[7:0] = {TEN_H, TEN_L}

  // Notes on the sheet:
  //   contents of rom_1 (hex, n*v repeats v):
  //   7e 12 bc b6 d2 e6 ee 72 fe f6 7e 12 bc b6 d2 e6 ee 72 fe f6 7e 12 bc b6 d2 e6 ee 72 fe f6 7e 12 bc
  //   b6 d2 e6 ee 72 fe f6 7e 12 bc b6 d2 e6 ee 72 fe f6 7e 12 bc b6 d2 e6 ee 72 fe f6 7e 12 bc b6 d2 e6
  //   ee 72 fe f6 7e 12 bc b6 d2 e6 ee 72 fe f6 7e 12 bc b6 d2 e6 ee 72 fe f6 7e 12 bc b6 d2 e6 ee 72 fe
  //   f6 7e 12 bc b6 d2 e6 ee 72 fe f6 7e 12 bc b6 d2 e6 ee 72 fe f6 7e 12 bc b6 d2 e6 ee 72 fe f6 7e 12
  //   bc b6 d2 e6 ee 72 fe f6 7e 12 bc b6 d2 e6 ee 72 fe f6 7e 12 bc b6 d2 e6 ee 72 fe f6 7e 12 bc b6 d2
  //   e6 ee 72 fe f6 7e 12 bc b6 d2 e6 ee 72 fe f6 7e 12 bc b6 d2 e6 ee 72 fe f6 7e 12 bc b6 d2 e6 ee 72
  //   fe f6 7e 12 bc b6 d2 e6 ee 72 fe f6 7e 12 bc b6 d2 e6 ee 72 fe f6 7e 12 bc b6 d2 e6 ee 72 fe f6 7e
  //   12 bc b6 d2 e6 ee 72 fe f6 7e 12 bc b6 d2 e6 ee 72 fe f6 7e 12 bc b6 d2 e6
  //   contents of rom_2 (hex, n*v repeats v):
  //   10*7e 10*12 10*bc 10*b6 10*d2 10*e6 10*ee 10*72 10*fe 10*f6 10*7e 10*12 10*bc 10*b6 10*d2 10*e6
  //   10*ee 10*72 10*fe 10*f6 10*7e 10*12 10*bc 10*b6 10*d2 6*e6
  //   contents of rom_3 (hex, n*v repeats v):
  //   100*7e 100*12 56*bc
  //   ONE_L
endmodule

module CPU_REGS (
  input  [15:0] in_1,
  input  [3:0] R_S,
  input  [3:0] R_E,
  input  FLAG_BUS_I,
  input  [3:0] FLAG_I,
  output [15:0] out_6,
  output [15:0] out_7,
  output [15:0] out_8,
  output [15:0] out_9,
  output [15:0] out_10,
  output [15:0] out_11,
  output [15:0] out_12,
  output [15:0] out_13,
  output [15:0] out_14,
  output [15:0] out_15,
  output [15:0] out_16,
  output [15:0] out_17,
  output [3:0] FLAG_O,
  output [15:0] out_19,
  output [15:0] out_20
);

  wire decoder_1_out1, decoder_1_out2, decoder_1_out3, decoder_1_out4, decoder_1_out5, decoder_1_out6,
       decoder_1_out7, decoder_1_out8, decoder_1_out9, decoder_1_out10, decoder_1_out11, decoder_1_out12,
       decoder_1_out13, decoder_2_out1, decoder_2_out2, decoder_2_out3, decoder_2_out4, decoder_2_out5,
       decoder_2_out6, decoder_2_out7, decoder_2_out8, decoder_2_out9, decoder_2_out10, decoder_2_out11,
       decoder_2_out12, decoder_2_out13, not_1_out;
  wire [15:0] multiplexer_1_out;

  Decoder #(.select(4)) decoder_1 (
    .out1(decoder_1_out1), .out2(decoder_1_out2), .out3(decoder_1_out3), .out4(decoder_1_out4),
    .out5(decoder_1_out5), .out6(decoder_1_out6), .out7(decoder_1_out7), .out8(decoder_1_out8),
    .out9(decoder_1_out9), .out10(decoder_1_out10), .out11(decoder_1_out11), .out12(decoder_1_out12),
    .out13(decoder_1_out13), .sel(R_S), .en(1'b1));  // open: out0, out14, out15
  not not_1 (not_1_out, FLAG_BUS_I);
  Multiplexer #(.width(16)) multiplexer_1 (
    .in0(in_1), .in1({{12{1'b0}}, FLAG_I}), .out(multiplexer_1_out), .sel(not_1_out));  // open: en
  CPU_R cpu_r_1 (.in_1(in_1), .out_5(out_6), .in_2(decoder_1_out1), .in_3(decoder_2_out1), .out_4(out_7));
  CPU_R cpu_r_2 (.in_1(in_1), .out_5(out_6), .in_2(decoder_1_out2), .in_3(decoder_2_out2), .out_4(out_8));
  CPU_R cpu_r_3 (.in_1(in_1), .out_5(out_6), .in_2(decoder_1_out3), .in_3(decoder_2_out3), .out_4(out_9));
  CPU_R cpu_r_4 (.in_1(in_1), .out_5(out_6), .in_2(decoder_1_out4), .in_3(decoder_2_out4), .out_4(out_10));
  CPU_R cpu_r_5 (.in_1(in_1), .out_5(out_6), .in_2(decoder_1_out5), .in_3(decoder_2_out5), .out_4(out_11));
  CPU_R cpu_r_6 (.in_1(in_1), .out_5(out_6), .in_2(decoder_1_out6), .in_3(decoder_2_out6), .out_4(out_12));
  CPU_R cpu_r_7 (.in_1(in_1), .out_5(out_6), .in_2(decoder_1_out7), .in_3(decoder_2_out7), .out_4(out_13));
  CPU_R cpu_r_8 (.in_1(in_1), .out_5(out_6), .in_2(decoder_1_out8), .in_3(decoder_2_out8), .out_4(out_14));
  CPU_R cpu_r_9 (.in_1(in_1), .out_5(out_6), .in_2(decoder_1_out9), .in_3(decoder_2_out9), .out_4(out_15));
  CPU_R cpu_r_10 (.in_1(in_1), .out_5(out_6), .in_2(decoder_1_out10), .in_3(decoder_2_out10), .out_4(out_16));
  CPU_R cpu_r_11 (.in_1(in_1), .out_5(out_6), .in_2(decoder_1_out11), .in_3(decoder_2_out11), .out_4(out_17));
  CPU_R cpu_r_12 (
    .in_1(multiplexer_1_out), .out_5(out_6), .in_2(decoder_1_out12), .in_3(decoder_2_out12),
    .out_4({out_19[15:4], FLAG_O}));
  CPU_R cpu_r_13 (.in_1(in_1), .out_5(out_6), .in_2(decoder_1_out13), .in_3(decoder_2_out13), .out_4(out_20));
  Decoder #(.select(4)) decoder_2 (
    .out1(decoder_2_out1), .out2(decoder_2_out2), .out3(decoder_2_out3), .out4(decoder_2_out4),
    .out5(decoder_2_out5), .out6(decoder_2_out6), .out7(decoder_2_out7), .out8(decoder_2_out8),
    .out9(decoder_2_out9), .out10(decoder_2_out10), .out11(decoder_2_out11), .out12(decoder_2_out12),
    .out13(decoder_2_out13), .sel(R_E), .en(1'b1));  // open: out0, out14, out15

  assign out_19[3:0] = FLAG_O;

  // Notes on the sheet:
  //   R_S: pull=down
  //   FLAG_BUS_I: pull=down
  //   R_E: pull=down
  //   FLAG_I: pull=down
  //   R_BUS_IN
  //   R1
  //   R2
  //   R3
  //   R4
  //   R5
  //   R6
  //   R7
  //   R8
  //   R9=LR
  //   R10=SP0
  //   R11=SP1
  //   R12=FLAG
  //   R13
  //   `
  //   R_BUS_OUT
endmodule

module RAM_WRITER (
  input  in_1,
  input  in_2,
  output [15:0] out_3,
  output [15:0] out_4,
  output out_5
);

  Counter #(.width(16), .max('hffff)) counter_1 (
    .count(1'b1), .Q(out_3), .clk(in_2), .clr(in_1));  // open: load, D, carry
  not not_1 (out_5, in_2);
  ROM #(.addrWidth(16), .dataWidth(16)) rom_1 (.addr(out_3), .data(out_4));  // open: sel

  // Notes on the sheet:
  //   contents of rom_1 (hex, n*v repeats v):
  //   2544 333 0 0 0 dddd 0 ffff 10*0 1111 111 0 0 0 ffff 30*0 ffff 0 0 0 cccc 0 eeee 12*0 dd 0 0 dd 0 0 0
  //   dd 75*0 dddd 15*0 3333 25*0 ddd 30*0 333 16*0 ddd 32*0 dd 519*0 3333
endmodule

module CPU_REG_4 (
);

  wire [15:0] cpu_register_16_1_out_4, undriven;

  CPU_REGISTER_16 cpu_register_16_1 (.in_1(undriven), .out_4(cpu_register_16_1_out_4));  // open: s, e, out_5
endmodule
